# Fritzing sketch Arduino_Pro_Mini_3V3 (saved by Fritzing 0.7.5b)
breadboards: 1

parts:
  Part1 = Arduino Pro Mini 3.3V
  BATT1 = 4xAA Switchable Battery Pack w/Bare Wire
  J1 = Basic Servo

nets:
  N1: Part1.RAW, BATT1.POS
  GND: Part1.GND, BATT1.NEG, J1.gnd
  N2: Part1.D3, J1.pulse

custom parts:
  4xAA Switchable Battery Pack w/Bare Wire: 4xAA Switchable Battery Pack with Bare Wire connection
